// Digital circuit 01.dig as structural Verilog
module _01 (
  input  [3:0] In,
  output A,
  output B,
  output C,
  output D,
  output E,
  output F,
  output G
);

  SixteenSeg sixteenseg_1 ();  // open: led, dp
  Seven_Seg seven_seg_1 ();  // open: a, b, c, d, e, f, g, dp
endmodule
