// Digital circuit BlockB.dig as structural Verilog
module BlockB (
  input  C1,
  input  C2,
  input  C3,
  output [6:0] Out
);

  wire not_1_out, not_2_out, not_3_out;

  not not_1 (not_1_out, C1);
  not not_2 (not_2_out, C2);
  not not_3 (not_3_out, C3);
  and and_1 (Out[6], not_1_out, not_2_out, C3);
  and and_2 (Out[5], not_1_out, C2, not_3_out);
  and and_3 (Out[4], not_1_out, C2, C3);
  and and_4 (Out[3], C1, not_2_out, not_3_out);
  and and_5 (Out[2], C1, not_2_out, C3);
  and and_6 (Out[1], C1, C2, not_3_out);
  and and_7 (Out[0], C1, C2, C3);
endmodule
